# Fritzing sketch raspi_red_led (saved by Fritzing 0.8.7b)
breadboards: 1

parts:
  RaspberryPi1 = Raspberry Pi Model B
  R1 = Resistor [tolerance=±5% resistance=220 package=THT]
  LED1 = LEDs [package=led10mm]

nets:
  N1: RaspberryPi1.SCL, RaspberryPi1.GND, RaspberryPi1.TXD, R1.Pin_0
  N2: RaspberryPi1.#22, RaspberryPi1.#23, RaspberryPi1.#24, LED1.C
  N3: R1.Pin_1, LED1.A

custom parts:
  Raspberry Pi Model B: Raspberry Pi (Model B)
