# Fritzing sketch raspi_rgb_led (saved by Fritzing 0.8.7b)
circuit board: 8.46667cm x 5.64444cm
breadboards: 1

parts:
  RaspberryPi1 = Raspberry Pi Model B
  LED1 = RGB LED - (4 legs) [package="5 mm [THT]"]
  R1 = Resistor [tolerance=±5% resistance=220 package=THT]
  R2 = Resistor [tolerance=±5% resistance=220 package=THT]
  R3 = Resistor [tolerance=±5% resistance=220 package=THT]

nets:
  N1: RaspberryPi1.5V, LED1.common_anode
  N2: RaspberryPi1.#23, R1.Pin_1
  N3: RaspberryPi1.#24, R2.Pin_1
  N4: RaspberryPi1.#25, R3.Pin_1
  N5: LED1.red_cathode, R1.Pin_0
  N6: LED1.green_cathode, R2.Pin_0
  N7: LED1.blue_cathode, R3.Pin_0

custom parts:
  Raspberry Pi Model B: Raspberry Pi (Model B)
